# Fritzing sketch microwave_schematic (saved by Fritzing 0.9.3b)

parts:
  Part2 = Arduino Uno (Rev3)
  SM1 = 28BYJ-48 Stepper Motor [part_number=28BYJ-48]
  Driver1 = 28BYJ-48 Driver Module [part_number=ULN2003 package=THT]
  Part3 = TXB0108 8-channel Bi-directional Logic Level Converter
  U4 = LM2596 step down module
  LCD1 = TFT 1.8 inch 160x128 w SD
  L1 = Solenoid
  Sensor1 = TTP223B Capacitive Touch Sensor Module
  Sensor2 = TTP223B Capacitive Touch Sensor Module
  Sensor3 = TTP223B Capacitive Touch Sensor Module
  Sensor4 = TTP223B Capacitive Touch Sensor Module
  Sensor5 = TTP223B Capacitive Touch Sensor Module
  Sensor6 = TTP223B Capacitive Touch Sensor Module
  Sensor7 = TTP223B Capacitive Touch Sensor Module
  Sensor8 = TTP223B Capacitive Touch Sensor Module
  Sensor9 = TTP223B Capacitive Touch Sensor Module
  Sensor10 = TTP223B Capacitive Touch Sensor Module
  Sensor11 = TTP223B Capacitive Touch Sensor Module
  Sensor12 = TTP223B Capacitive Touch Sensor Module
  Sensor13 = TTP223B Capacitive Touch Sensor Module
  Sensor14 = TTP223B Capacitive Touch Sensor Module
  Sensor15 = TTP223B Capacitive Touch Sensor Module
  Sensor16 = TTP223B Capacitive Touch Sensor Module
  Sensor17 = TTP223B Capacitive Touch Sensor Module
  Sensor18 = TTP223B Capacitive Touch Sensor Module
  Sensor19 = TTP223B Capacitive Touch Sensor Module
  Sensor20 = TTP223B Capacitive Touch Sensor Module
  Sensor21 = TTP223B Capacitive Touch Sensor Module
  Sensor22 = TTP223B Capacitive Touch Sensor Module
  J3 = 2.1mm Barrel Jack with Terminal Block
  KY-1 = Keyes Relay [package=THT]
  J4 = Piezo Speaker
  R1 = Resistor [tolerance=±5% resistance=1k package="2512 [SMD]"]
  PCB2 = RTC_DS1302_module
  USBTTL1 = USB A Plug
  USBTTL2 = Micro USB B Plug
  Mod1 = Raspberry Pi 4B

nets:
  N1: Part2.A3, PCB2.RST
  N2: Part2.A4/SDA, PCB2.DAT
  N3: Part2.A5/SCL, PCB2.CLK
  N4: Part2.D8, Part3.B3
  N5: Part2.D9_PWM, Part3.B4
  N6: Part2.D10_PWM/SS, Part3.B5
  N7: Part2.D11_PWM/MOSI, Part3.B2
  N8: Part2.D13/SCK, Part3.B1
  N9: Part2.D2, KY-1.signal
  N10: Part2.D3_PWM, J4.pin2
  N11: Part2.D4, Driver1.IN4
  N12: Part2.D5_PWM, Driver1.IN3
  N13: Part2.D6_PWM, Driver1.IN2
  N14: Part2.D7, Driver1.IN1
  N15: Part2.3V3, Part3.VCCA, R1.Pin_0
  5V: Part2.5V, PCB2.VCC
  GND: Part2.GND, PCB2.GND
  N16: SM1.blue-pin, Driver1.blue-pin
  N17: SM1.pink-pin, Driver1.pink-pin
  N18: SM1.yellow-pin, Driver1.yellow-pin
  N19: SM1.orange-pin, Driver1.orange-pin
  N20: SM1.red-pin, Driver1.red-pin
  N21: Part3.OE, R1.Pin_1
  N22: Part3.A5, LCD1.pin2
  N23: Part3.A4, LCD1.pin3
  N24: Part3.A3, LCD1.pin4
  N25: Part3.A2, LCD1.pin_5
  N26: Part3.A1, LCD1.pin_6
  N27: U4.IN+, J3.POS
  N28: U4.IN-, U4.OUT-, J3.NEG, KY-1.ground
  N29: U4.OUT+, KY-1.power
  N30: L1.pin1, KY-1.C
  GND_2: Sensor1.GND, Sensor2.GND, Sensor3.GND
  VCC: Sensor1.VCC, Sensor2.VCC, Sensor3.VCC
  N31: Sensor1.SIG, Mod1.GPIO19
  N32: Sensor2.SIG, Mod1.GPIO7
  N33: Sensor3.SIG, Mod1.GPIO9
  GND_3: Sensor4.GND, Sensor5.GND
  VCC_2: Sensor4.VCC, Sensor5.VCC
  N34: Sensor4.SIG, Mod1.GPIO16
  N35: Sensor5.SIG, Mod1.GPIO13
  GND_4: Sensor6.GND, Sensor7.GND, Sensor9.GND
  VCC_3: Sensor6.VCC, Sensor7.VCC, Sensor9.VCC
  N36: Sensor6.SIG, Mod1.GPIO10
  N37: Sensor7.SIG, Mod1.GPIO17
  GND_5: Sensor8.GND, Sensor11.GND, Sensor12.GND
  VCC_4: Sensor8.VCC, Sensor11.VCC, Sensor12.VCC
  N38: Sensor8.SIG, Mod1.GPIO5
  N39: Sensor9.SIG, Mod1.GPIO11
  GND_6: Sensor10.GND, Sensor13.GND, Sensor14.GND
  VCC_5: Sensor10.VCC, Sensor13.VCC, Sensor14.VCC
  N40: Sensor10.SIG, Mod1.GPIO20
  N41: Sensor11.SIG, Mod1.GPIO25
  N42: Sensor12.SIG, Mod1.GPIO21
  N43: Sensor13.SIG, Mod1.GPIO3
  N44: Sensor14.SIG, Mod1.GPIO12
  GND_7: Sensor15.GND, Sensor16.GND, Sensor17.GND, Sensor18.GND
  VCC_6: Sensor15.VCC, Sensor16.VCC, Sensor17.VCC, Sensor18.VCC
  N45: Sensor15.SIG, Mod1.GPIO24
  N46: Sensor16.SIG, Mod1.GPIO26
  N47: Sensor17.SIG, Mod1.GPIO4
  N48: Sensor18.SIG, Mod1.GPIO22
  GND_8: Sensor19.GND, Sensor20.GND
  VCC_7: Sensor19.VCC, Sensor20.VCC
  N49: Sensor19.SIG, Mod1.GPIO8
  N50: Sensor20.SIG, Mod1.GPIO27
  GND_9: Sensor21.GND, Sensor22.GND
  VCC_8: Sensor21.VCC, Sensor22.VCC
  N51: Sensor21.SIG, Mod1.GPIO2
  N52: Sensor22.SIG, Mod1.GPIO6
  N53: USBTTL1.usb, USBTTL2.usb

notes:
  1
  2
  3
  4
  5
  6
  7
  8
  9
  10
  11
  12
  13
  14
  15
  16
  17
  18
  19
  20
  21
  22

custom parts:
  28BYJ-48 Stepper Motor: Unipolar Stepper Motor 28BYJ-48 Top coil - pink & orange Bottom coil - blue & yellow Common rail - red Connector pins: blue - pink - yellow - orange - red
  28BYJ-48 Driver Module: High-power ULN2003 Stepper Motor Driver Board Test Module For Arduino AVR SMD
  TXB0108 8-channel Bi-directional Logic Level Converter: Because the Arduino (and Basic Stamp) are 5V devices, and most modern sensors, displays, flash cards and modes are 3.3V-only, many makers find that they need to perform level shifting/conversion to protect the 3.3V device from 5V. Although one can use resistors to make a divider, for high speed transfers, the resistors can add a lot of slew and cause havoc that is tough to debug. For that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
  LM2596 step down module: LM2596 DC-DC step down power supply module 3 A.
  TFT 1.8 inch 160x128 w SD: This is a generic 1.8 tft spi lcd display available on ebay and others. The 1.8" display has 128x160 color pixels and in this version pin names in breadboard (unlike the real board).
  TTP223B Capacitive Touch Sensor Module: The TTP223B capacitive touch sensor module uses the TTP223B IC. The appropriate voltage is approximately 2 to 5.5 volts.
  Keyes Relay: The Keyes 5V relay module is suitable for SCM development, home appliance control. It uses a 5V~12V TIL control signal which can control DC / AC signal.
  RTC_DS1302_module: Arduino module DS1302 SPI Real Time Clock
